// Logisim project FULL ADDER-ADDERS.circ as structural Verilog: 1 circuit, main circuit main
module main (
  input  A,
  input  A_2,
  input  B,
  input  B_2,
  input  C,
  input  C_2,
  output out_7,
  output out_8
);

  wire A___B_out, A___C_out, B___C_out, xor_1_out;

  xor xor_1 (xor_1_out, A_2, B_2);
  xor xor_2 (out_7, xor_1_out, C);
  and A___B (A___B_out, A, A);
  and B___C (B___C_out, A, C_2);
  and A___C (A___C_out, A, C_2);
  or or_1 (out_8, A___B_out, B___C_out, A___C_out);

  assign B = A;

  // Notes on the sheet:
  //   Sum = A XOR B XOR Gate
  //   FULL ADDERS
  //   Carry = (A AND B) OR ( B AND C) OR ( A AND C)
endmodule
