// Logisim project Half-ADDERS.circ as structural Verilog: 1 circuit, main circuit main
module main (
  input  A,
  input  A_2,
  input  B,
  input  B_2,
  output out_5,
  output out_6
);

  xor xor_1 (out_5, A, B);
  and and_1 (out_6, A_2, B_2);

  // Notes on the sheet:
  //   Sum = A XOR -> use XOR Gate
  //   HALF ADDERS
  //   Carrry = ( A AND B ) OR ( B AND C) OR ( A AND C)
endmodule
